// Logisim project 16Bit_Computer.circ as structural Verilog: 4 circuits, main circuit ALU
module ALU (
  input  zero_x,
  input  not_x,
  input  zero_y,
  input  not_y,
  input  funtion,
  input  not_output,
  input  [15:0] x,
  input  [15:0] y,
  output [15:0] op,
  output zero,
  output negative
);

  wire not_1_out, not_2_out, not_7_out;
  wire [15:0] adder_1_out, and_1_out, and_2_out, and_3_out, and_4_out, and_5_out, and_6_out, and_7_out,
       and_8_out, and_9_out, and_10_out, and_11_out, bit_extender_1_out, bit_extender_2_out,
       bit_extender_3_out, bit_extender_4_out, bit_extender_5_out, bit_extender_6_out, bit_extender_7_out,
       not_3_out, not_4_out, not_5_out, not_6_out, not_8_out, not_9_out, or_1_out, or_2_out, or_3_out;

  not not_1 (not_1_out, zero_x);
  not not_2 (not_2_out, zero_y);
  assign bit_extender_1_out = {{15{not_1_out}}, not_1_out};  // Bit_Extender bit_extender_1
  assign bit_extender_2_out = {{15{not_2_out}}, not_2_out};  // Bit_Extender bit_extender_2
  assign and_1_out = bit_extender_1_out & x;  // AND_Gate and_1, 16 bits wide
  assign bit_extender_3_out = {{15{not_x}}, not_x};  // Bit_Extender bit_extender_3
  assign and_2_out = bit_extender_2_out & y;  // AND_Gate and_2, 16 bits wide
  assign bit_extender_4_out = {{15{not_y}}, not_y};  // Bit_Extender bit_extender_4
  assign not_3_out = ~bit_extender_3_out;  // NOT_Gate not_3, 16 bits wide
  assign not_4_out = ~and_1_out;  // NOT_Gate not_4, 16 bits wide
  assign not_5_out = ~bit_extender_4_out;  // NOT_Gate not_5, 16 bits wide
  assign not_6_out = ~and_2_out;  // NOT_Gate not_6, 16 bits wide
  assign and_3_out = and_1_out & not_3_out;  // AND_Gate and_3, 16 bits wide
  assign and_4_out = bit_extender_3_out & not_4_out;  // AND_Gate and_4, 16 bits wide
  assign and_5_out = and_2_out & not_5_out;  // AND_Gate and_5, 16 bits wide
  assign and_6_out = bit_extender_4_out & not_6_out;  // AND_Gate and_6, 16 bits wide
  assign or_1_out = and_3_out | and_4_out;  // OR_Gate or_1, 16 bits wide
  assign or_2_out = and_5_out | and_6_out;  // OR_Gate or_2, 16 bits wide
  assign and_7_out = or_1_out & or_2_out;  // AND_Gate and_7, 16 bits wide
  Adder #(.width(16)) adder_1 (.a(or_1_out), .b(or_2_out), .out(adder_1_out));  // open: cin, cout
  assign bit_extender_5_out = {{15{not_7_out}}, not_7_out};  // Bit_Extender bit_extender_5
  not not_7 (not_7_out, funtion);
  assign bit_extender_6_out = {{15{funtion}}, funtion};  // Bit_Extender bit_extender_6
  assign and_8_out = bit_extender_5_out & and_7_out;  // AND_Gate and_8, 16 bits wide
  assign and_9_out = bit_extender_6_out & adder_1_out;  // AND_Gate and_9, 16 bits wide
  assign or_3_out = and_8_out | and_9_out;  // OR_Gate or_3, 16 bits wide
  assign not_8_out = ~or_3_out;  // NOT_Gate not_8, 16 bits wide
  assign bit_extender_7_out = {{15{not_output}}, not_output};  // Bit_Extender bit_extender_7
  assign not_9_out = ~bit_extender_7_out;  // NOT_Gate not_9, 16 bits wide
  assign and_10_out = bit_extender_7_out & not_8_out;  // AND_Gate and_10, 16 bits wide
  assign and_11_out = not_9_out & or_3_out;  // AND_Gate and_11, 16 bits wide
  assign op = and_10_out | and_11_out;  // OR_Gate or_4, 16 bits wide
  Comparator #(.width(16)) comparator_1 (.a(op), .b({16{1'b0}}), .eq(zero), .lt(negative));  // open: gt

  // Other names for the same wires on the sheet: f = funtion; ng = negative; no = not_output; nx = not_x; ny = not_y;
  //   zr = zero; zx = zero_x; zy = zero_y
endmodule

module PC (
  input  increment,
  input  load,
  input  reset,
  input  [15:0] i,
  input  clock,
  output [15:0] o
);

  wire or_1_out;
  wire [15:0] adder_1_out, multiplexer_1_out, multiplexer_2_out, multiplexer_3_out;

  Multiplexer #(.width(16)) multiplexer_1 (
    .in0({16{1'b0}}), .in1(adder_1_out), .out(multiplexer_1_out), .sel(increment));
  Multiplexer #(.width(16)) multiplexer_2 (.in0(multiplexer_1_out), .in1(i), .out(multiplexer_2_out), .sel(load));
  or or_1 (or_1_out, reset, load, increment);
  Multiplexer #(.width(16)) multiplexer_3 (
    .in0(multiplexer_2_out), .in1({16{1'b0}}), .out(multiplexer_3_out), .sel(reset));
  Register #(.width(16)) register_1 (.D(multiplexer_3_out), .en(or_1_out), .clk(clock), .Q(o));  // open: clr
  Adder #(.width(16)) adder_1 (.a(o), .b(16'h1), .out(adder_1_out));  // open: cin, cout
endmodule

module CPU (
  input  [15:0] Instruction,
  input  [15:0] inM,
  input  reset,
  input  clock,
  output [15:0] outM,
  output writeM,
  output [15:0] addressM,
  output [15:0] pcOut
);

  wire and_1_out, and_2_out, and_3_out, and_4_out, and_5_out, and_6_out, and_7_out, and_8_out, and_9_out,
       and_10_out, and_11_out, and_12_out, ng, not_1_out, not_2_out, not_3_out, not_4_out, not_5_out,
       not_6_out, not_7_out, not_8_out, not_9_out, not_10_out, not_11_out, not_12_out, not_13_out,
       not_14_out, not_15_out, not_16_out, not_17_out, or_1_out, or_2_out, or_3_out, or_4_out, zr;
  wire [15:0] DR_q, multiplexer_1_out, multiplexer_2_out;

  Multiplexer #(.width(16)) multiplexer_1 (
    .in0(Instruction), .in1(outM), .out(multiplexer_1_out), .sel(Instruction[15]));
  not not_1 (not_1_out, ng);
  and and_1 (and_1_out, Instruction[15], Instruction[5]);
  not not_2 (not_2_out, Instruction[15]);
  or or_1 (or_1_out, zr, not_1_out);
  and and_2 (and_2_out, Instruction[4], Instruction[15]);
  or or_2 (or_2_out, and_1_out, not_2_out);
  not not_3 (not_3_out, Instruction[2]);
  not not_4 (not_4_out, Instruction[1]);
  not not_5 (not_5_out, zr);
  not not_6 (not_6_out, ng);
  not not_7 (not_7_out, Instruction[2]);
  not not_8 (not_8_out, Instruction[0]);
  not not_9 (not_9_out, Instruction[2]);
  not not_10 (not_10_out, Instruction[1]);
  not not_11 (not_11_out, Instruction[0]);
  not not_12 (not_12_out, zr);
  Register #(.width(16)) DR (.D(outM), .en(and_2_out), .clk(clock), .Q(DR_q));  // open: clr
  Register #(.width(16)) AR (.D(multiplexer_1_out), .en(or_2_out), .clk(clock), .Q(addressM));  // open: clr
  and and_3 (and_3_out, not_3_out, not_4_out, Instruction[0], not_5_out, not_6_out);
  and and_4 (and_4_out, not_7_out, Instruction[1], not_8_out, zr);
  and and_5 (and_5_out, not_9_out, Instruction[1], Instruction[0], or_1_out);
  and and_6 (and_6_out, Instruction[2], not_10_out, not_11_out, not_12_out, ng);
  or or_3 (or_3_out, zr, ng);
  not not_13 (not_13_out, Instruction[1]);
  not not_14 (not_14_out, zr);
  not not_15 (not_15_out, Instruction[0]);
  and and_7 (and_7_out, Instruction[12], Instruction[15]);
  and and_8 (and_8_out, Instruction[2], not_13_out, Instruction[0], not_14_out);
  and and_9 (and_9_out, Instruction[2], Instruction[1], not_15_out, or_3_out);
  and and_10 (and_10_out, Instruction[2], Instruction[1], Instruction[0]);
  Multiplexer #(.width(16)) multiplexer_2 (.in0(addressM), .in1(inM), .out(multiplexer_2_out), .sel(and_7_out));
  or or_4 (or_4_out, and_3_out, and_8_out, and_4_out, and_9_out, and_5_out, and_10_out, and_6_out);
  and and_11 (and_11_out, Instruction[15], or_4_out);
  not not_16 (not_16_out, reset);
  not not_17 (not_17_out, and_11_out);
  and and_12 (and_12_out, not_16_out, not_17_out);
  PC pc_1 (.i(addressM), .clock(clock), .increment(and_12_out), .load(and_11_out), .reset(reset), .o(pcOut));
  ALU alu_1 (
    .not_output(Instruction[6]), .x(DR_q), .y(multiplexer_2_out), .zero_x(Instruction[11]),
    .not_x(Instruction[10]), .zero_y(Instruction[9]), .not_y(Instruction[8]), .funtion(Instruction[7]),
    .op(outM), .zero(zr), .negative(ng));
  and and_13 (writeM, Instruction[3], Instruction[15]);

  // Other names for the same wires on the sheet: aluOut[15:0] = outM; clk = clock; j1 = Instruction[0];
  //   j2 = Instruction[1]; j3 = Instruction[2]; d1 = Instruction[3]; d2 = Instruction[4]; d3 = Instruction[5];
  //   c1 = Instruction[6]; c2 = Instruction[7]; c3 = Instruction[8]; c4 = Instruction[9]; c5 = Instruction[10];
  //   c6 = Instruction[11]; a = Instruction[12]; i1 = Instruction[13]; i2 = Instruction[14]; A_C = Instruction[15];
  //   outA[15:0] = addressM
endmodule

module Computer (
  input  Reset
);

  wire clock_1_out, clock_2_out, cpu_1_writem;
  wire [14:0] bit_extender_1_out, bit_extender_2_out;
  wire [15:0] cpu_1_addressm, cpu_1_outm, cpu_1_pcout, ram_1_dout, rom_1_data;

  ROM #(.addrWidth(15), .dataWidth(16)) rom_1 (.addr(bit_extender_2_out), .data(rom_1_data));
  Clock clock_1 (.out(clock_1_out));
  CPU cpu_1 (
    .reset(Reset), .clock(clock_1_out), .Instruction(rom_1_data), .inM(ram_1_dout),
    .addressM(cpu_1_addressm), .pcOut(cpu_1_pcout), .outM(cpu_1_outm), .writeM(cpu_1_writem));
  Bit_Extender #(.in_width(16), .out_width(15)) bit_extender_1 (.in(cpu_1_addressm), .out(bit_extender_1_out));
  Bit_Extender #(.in_width(16), .out_width(15)) bit_extender_2 (.in(cpu_1_pcout), .out(bit_extender_2_out));
  RAM #(.addrWidth(15), .dataWidth(16), .enables("line")) ram_1 (
    .addr(bit_extender_1_out), .we(cpu_1_writem), .clk(clock_2_out), .din(cpu_1_outm), .dout(ram_1_dout));
  Clock clock_2 (.out(clock_2_out));
endmodule
